// Logisim project cpu_project.circ as structural Verilog: 7 circuits, main circuit project_ao
module project_ao (
  input  [15:0] INPUT_A,
  input  Borrow_in,
  input  carry_in,
  input  [15:0] INPUT_B,
  input  [3:0] OP_CODE,
  output Borrow_out,
  output carry_out,
  output [15:0] ADD_OUT,
  output [15:0] SUB_OUT,
  output [15:0] MULT_OUT,
  output [15:0] Data_out,
  output [15:0] DIV_OUT,
  output [15:0] EXPO_OUT,
  output [15:0] AND_OUT,
  output [15:0] OR_OUT,
  output [15:0] NOT_OUT,
  output [15:0] XOR_OUT,
  output [15:0] NOR_OUT,
  output [15:0] B_L2,
  output [15:0] A_L2,
  output [15:0] B_R2,
  output [15:0] A_R2,
  output [15:0] COMP_B,
  output [15:0] COMP_A,
  output Zero_Flag
);

  wire and_2_out, and_3_out, and_4_out, and_5_out, and_6_out, and_7_out, and_8_out, and_9_out, and_10_out,
       and_11_out, and_12_out, and_13_out, and_14_out, and_15_out, not_2_out, not_3_out, not_4_out,
       not_5_out, not_6_out, not_7_out, not_8_out, not_9_out, not_10_out, not_11_out, not_12_out, not_13_out,
       not_14_out, not_15_out, not_16_out, not_17_out;
  wire [15:0] or_2_out;

  Subtractor #(.width(16)) subtractor_1 (.a(INPUT_B), .b(INPUT_A), .out(SUB_OUT), .bin(Borrow_in), .bout(Borrow_out));
  Adder #(.width(16)) adder_1 (.a(INPUT_A), .b(INPUT_B), .out(ADD_OUT), .cin(carry_in), .cout(carry_out));
  Multiplier #(.width(16)) multiplier_1 (.a(INPUT_B), .b(INPUT_A), .out(MULT_OUT));  // open: cin, cout
  Divider #(.width(16)) divider_1 (.a(INPUT_B), .b(INPUT_A), .out(DIV_OUT));  // open: upper, rem
  // Exponentiator #(.width(16)) exponentiator_1: pin names not known; wires that end beside it: INPUT_B, INPUT_A, EXPO_OUT
  assign AND_OUT = INPUT_B & INPUT_A;  // AND_Gate and_1, 16 bits wide
  assign OR_OUT = INPUT_B | INPUT_A;  // OR_Gate or_1, 16 bits wide
  assign NOT_OUT = ~INPUT_A;  // NOT_Gate not_1, 16 bits wide
  assign XOR_OUT = INPUT_B ^ INPUT_A;  // XOR_Gate xor_1, 16 bits wide
  assign NOR_OUT = ~(INPUT_B | INPUT_A);  // NOR_Gate nor_1, 16 bits wide
  Shifter #(.width(16)) shifter_1 (.in(INPUT_B), .\dist (4'b0010), .out(B_L2));
  Shifter #(.width(16)) shifter_2 (.in(INPUT_A), .\dist (4'b0010), .out(A_L2));
  Shifter #(.shift("lr"), .width(16)) shifter_3 (.in(INPUT_B), .\dist (4'b0010), .out(B_R2));
  Shifter #(.shift("lr"), .width(16)) shifter_4 (.in(INPUT_A), .\dist (4'b0010), .out(A_R2));
  Negator #(.width(16)) negator_1 (.in(INPUT_B), .out(COMP_B));
  Negator #(.width(16)) negator_2 (.in(INPUT_A), .out(COMP_A));
  Multiplexer #(.select(4), .width(16)) multiplexer_1 (
    .in0(ADD_OUT), .in1(SUB_OUT), .in2(MULT_OUT), .in3(DIV_OUT), .in4(EXPO_OUT), .in5(AND_OUT), .in6(OR_OUT),
    .in7(NOT_OUT), .in8(XOR_OUT), .in9(NOR_OUT), .in10(B_L2), .in11(A_L2), .in12(B_R2), .in13(A_R2),
    .in14(COMP_B), .in15(COMP_A), .out(Data_out), .sel(OP_CODE));
  assign or_2_out = Data_out;  // OR_Gate or_2, 16 bits wide OR_Gate
  not not_2 (not_2_out, or_2_out[0]);
  not not_3 (not_3_out, or_2_out[1]);
  not not_4 (not_4_out, or_2_out[2]);
  and and_2 (and_2_out, not_2_out, not_3_out);
  and and_3 (and_3_out, and_2_out, not_4_out);
  not not_5 (not_5_out, or_2_out[3]);
  not not_6 (not_6_out, or_2_out[4]);
  not not_7 (not_7_out, or_2_out[5]);
  not not_8 (not_8_out, or_2_out[6]);
  and and_4 (and_4_out, and_3_out, not_5_out);
  and and_5 (and_5_out, and_4_out, not_6_out);
  and and_6 (and_6_out, and_5_out, not_7_out);
  not not_9 (not_9_out, or_2_out[7]);
  not not_10 (not_10_out, or_2_out[8]);
  not not_11 (not_11_out, or_2_out[9]);
  and and_7 (and_7_out, and_6_out, not_8_out);
  and and_8 (and_8_out, and_7_out, not_9_out);
  not not_12 (not_12_out, or_2_out[10]);
  not not_13 (not_13_out, or_2_out[11]);
  not not_14 (not_14_out, or_2_out[12]);
  not not_15 (not_15_out, or_2_out[13]);
  and and_9 (and_9_out, and_8_out, not_10_out);
  and and_10 (and_10_out, and_9_out, not_11_out);
  and and_11 (and_11_out, and_10_out, not_12_out);
  not not_16 (not_16_out, or_2_out[14]);
  not not_17 (not_17_out, or_2_out[15]);
  and and_12 (and_12_out, and_11_out, not_13_out);
  and and_13 (and_13_out, and_12_out, not_14_out);
  and and_14 (and_14_out, and_13_out, not_15_out);
  and and_15 (and_15_out, and_14_out, not_16_out);
  and and_16 (Zero_Flag, and_15_out, not_17_out);
  Pull_Resistor pull_resistor_1 (.node(or_2_out[0]));
  Pull_Resistor pull_resistor_2 (.node(or_2_out[1]));
  Pull_Resistor pull_resistor_3 (.node(or_2_out[2]));
  Pull_Resistor pull_resistor_4 (.node(or_2_out[3]));
  Pull_Resistor pull_resistor_5 (.node(or_2_out[4]));
  Pull_Resistor pull_resistor_6 (.node(or_2_out[5]));
  Pull_Resistor pull_resistor_7 (.node(or_2_out[6]));
  Pull_Resistor pull_resistor_8 (.node(or_2_out[7]));
  Pull_Resistor pull_resistor_9 (.node(or_2_out[8]));
  Pull_Resistor pull_resistor_10 (.node(or_2_out[9]));
  Pull_Resistor pull_resistor_11 (.node(or_2_out[10]));
  Pull_Resistor pull_resistor_12 (.node(or_2_out[11]));
  Pull_Resistor pull_resistor_13 (.node(or_2_out[12]));
  Pull_Resistor pull_resistor_14 (.node(or_2_out[13]));
  Pull_Resistor pull_resistor_15 (.node(or_2_out[14]));
  Pull_Resistor pull_resistor_16 (.node(or_2_out[15]));
endmodule

module project_ro (
  input  [15:0] INPUT_A,
  input  NOTHING,
  input  [15:0] INPUT_B,
  input  [2:0] RUselect,
  output GREATER_THAN,
  output EQUAL,
  output LESSTHAN,
  output GREATER_EQUAL,
  output LESS_EQUAL,
  output RURESULT,
  output NOT_EQUAL
);

  Comparator #(.width(16)) comparator_1 (.a(INPUT_A), .b(INPUT_B), .gt(GREATER_THAN), .eq(EQUAL), .lt(LESSTHAN));
  or or_1 (GREATER_EQUAL, GREATER_THAN, EQUAL);
  or or_2 (LESS_EQUAL, EQUAL, LESSTHAN);
  not not_1 (NOT_EQUAL, EQUAL);
  Multiplexer #(.select(3)) multiplexer_1 (
    .in0(GREATER_THAN), .in1(EQUAL), .in2(LESSTHAN), .in3(GREATER_EQUAL), .in4(LESS_EQUAL), .in5(NOT_EQUAL),
    .in6(NOTHING), .in7(NOTHING), .out(RURESULT), .sel(RUselect));
endmodule

module project_alu (
  input  NOTHING,
  input  [2:0] RO_SELECT,
  input  [15:0] INPUT_A,
  input  [15:0] INPUT_B,
  input  [3:0] OP_CODE,
  input  CARRY_IN,
  input  BORROW_IN,
  input  ALU_SELECTOR,
  input  AOEnable,
  output [15:0] RORESULT,
  output [15:0] FINAL_RESULT,
  output [15:0] AORESULT,
  output [15:0] AO_DOUT,
  output zeroflag
);

  project_ro project_ro_1 (
    .INPUT_A(INPUT_A), .NOTHING(NOTHING), .INPUT_B(INPUT_B), .RUselect(RO_SELECT), .RURESULT(RORESULT[0]));  // open: GREATER_THAN, EQUAL, LESSTHAN, GREATER_EQUAL, LESS_EQUAL, NOT_EQUAL
  project_ao project_ao_1 (
    .INPUT_A(INPUT_A), .Borrow_in(BORROW_IN), .carry_in(CARRY_IN), .INPUT_B(INPUT_B), .OP_CODE(OP_CODE),
    .Data_out(AORESULT), .Zero_Flag(zeroflag));  // open: Borrow_out, carry_out, ADD_OUT, SUB_OUT, MULT_OUT, DIV_OUT, EXPO_OUT, AND_OUT, OR_OUT, NOT_OUT, XOR_OUT, NOR_OUT, B_L2, A_L2, B_R2, A_R2, COMP_B, COMP_A
  assign AO_DOUT = AOEnable ? AORESULT : 16'bz;  // Controlled_Buffer controlled_buffer_1
  Multiplexer #(.width(16)) multiplexer_1 (
    .in0({{15{1'b0}}, RORESULT[0]}), .in1(AORESULT), .out(FINAL_RESULT), .sel(ALU_SELECTOR));

  assign RORESULT[15:1] = {15{1'b0}};
endmodule

module Datapath (
  input  [15:0] in_1,
  input  OE_TestingData,
  input  WE_MAR,
  input  RESET_MAR,
  input  OE_MAR,
  input  Internal_OE,
  input  WE_IR,
  input  WE_MBR,
  input  Reset_IR,
  input  RESET_MBR,
  input  OE_IR,
  input  OE_MBR,
  input  WE_A,
  input  WE_OR,
  input  RESET_OR,
  input  Reset_A,
  input  OE_OR,
  input  OE_A,
  input  [2:0] ro_selector,
  input  AO_Enable,
  input  [3:0] ao_selector,
  input  Borrow_in,
  input  Carry_in,
  input  Alu_selector,
  input  WE_B,
  input  Reset_B,
  input  OE_B,
  output [7:0] Content_MAR,
  output [15:0] Content_IR,
  output [15:0] Content_MBR,
  output [15:0] Dout_IR,
  output [15:0] Content_A,
  output [15:0] Content_Output,
  output [15:0] Dout_A,
  output [15:0] AUResult,
  output [15:0] Dout,
  output [15:0] RUResult,
  output [15:0] out_38,
  output [15:0] Content_B,
  output out_40,
  output [15:0] Dout_B
);

  wire CLK_out;
  wire [7:0] bitselector_1_out, controlled_buffer_6_out;

  Clock CLK (.out(CLK_out));
  Register #(.width(16)) Instruction_Register (.D(Dout), .en(WE_IR), .clk(CLK_out), .Q(Content_IR), .clr(Reset_IR));
  Register #(.width(16)) Register_A (.D(Dout), .en(WE_A), .clk(CLK_out), .Q(Content_A), .clr(Reset_A));
  Register #(.width(16)) Register_B (.D(Dout), .en(WE_B), .clk(CLK_out), .Q(Content_B), .clr(Reset_B));
  assign Dout_IR = OE_IR ? Content_IR : 16'bz;  // Controlled_Buffer controlled_buffer_1
  assign Dout_A = OE_A ? Content_A : 16'bz;  // Controlled_Buffer controlled_buffer_2
  assign Dout_B = OE_B ? Content_B : 16'bz;  // Controlled_Buffer controlled_buffer_3
  BitSelector #(.group(8), .width(16)) bitselector_1 (.in(Dout_IR), .out(bitselector_1_out), .sel(1'b0));
  LED D15 (.in(Dout[15]));
  LED D14 (.in(Dout[14]));
  LED D13 (.in(Dout[13]));
  LED D12 (.in(Dout[12]));
  LED D11 (.in(Dout[11]));
  assign Dout = OE_TestingData ? in_1 : 16'bz;  // Controlled_Buffer controlled_buffer_4
  LED D10 (.in(Dout[10]));
  LED D9 (.in(Dout[9]));
  LED D8 (.in(Dout[8]));
  LED D7 (.in(Dout[7]));
  LED D6 (.in(Dout[6]));
  LED D5 (.in(Dout[5]));
  LED D4 (.in(Dout[4]));
  LED D3 (.in(Dout[3]));
  LED D2 (.in(Dout[2]));
  LED D1 (.in(Dout[1]));
  LED D0 (.in(Dout[0]));
  project_alu project_alu_1 (
    .NOTHING(1'b0), .RO_SELECT(ro_selector), .INPUT_A(Content_A), .INPUT_B(Content_B), .OP_CODE(ao_selector),
    .CARRY_IN(Carry_in), .BORROW_IN(Borrow_in), .ALU_SELECTOR(Alu_selector), .AOEnable(AO_Enable),
    .RORESULT(RUResult), .FINAL_RESULT(AUResult), .AORESULT(out_38), .AO_DOUT(Dout), .zeroflag(out_40));
  Register Memory_Address_Register (
    .D(bitselector_1_out), .en(WE_MAR), .clk(CLK_out), .Q(Content_MAR), .clr(RESET_MAR));
  assign Dout = Internal_OE ? Content_MBR : 16'bz;  // Controlled_Buffer controlled_buffer_5
  Register #(.width(16)) Memory_Buffer_Register (
    .D(Dout), .en(WE_MBR), .clk(CLK_out), .Q(Content_MBR), .clr(RESET_MBR));
  Register #(.width(16)) Output_Register (.D(Dout), .en(WE_OR), .clk(CLK_out), .Q(Content_Output), .clr(RESET_OR));
  assign controlled_buffer_6_out = OE_MAR ? Content_MAR : 8'bz;  // Controlled_Buffer controlled_buffer_6
  assign Dout = OE_MBR ? Content_MBR : 16'bz;  // Controlled_Buffer controlled_buffer_7
  assign Dout = OE_OR ? Content_Output : 16'bz;  // Controlled_Buffer controlled_buffer_8
  LED led_1 (.in(Dout[15]));
  LED led_2 (.in(Dout[14]));
  LED led_3 (.in(Dout[13]));
  LED led_4 (.in(Dout[12]));
  LED led_5 (.in(Dout[11]));
  LED led_6 (.in(Dout[10]));
  LED led_7 (.in(Dout[9]));
  LED led_8 (.in(Dout[8]));
  LED led_9 (.in(Dout[7]));
  LED led_10 (.in(Dout[6]));
  LED led_11 (.in(Dout[5]));
  LED led_12 (.in(Dout[4]));
  LED led_13 (.in(Dout[3]));
  LED led_14 (.in(Dout[2]));
  LED led_15 (.in(Dout[1]));
  LED led_16 (.in(Dout[0]));
endmodule

module Decimaldecoder (
  input  [15:0] Din,
  output [31:0] Dout
);

  ROM #(.addrWidth(16), .dataWidth(32)) rom_1 (
    .addr(Din),
    .data({Dout[31:28], Dout[15:12], Dout[27:24], Dout[11:8], Dout[23:20], Dout[7:4], Dout[19:16], Dout[3:0]}));

  // Notes on the sheet:
  //   contents of rom_1 (hex, n*v repeats v):
  //   e7 21 cb 6b 2d 6e ee 23 ef 2f 21e7 2121 21cb 216b 212d 216e 21ee 2123 21ef 212f cbe7 cb21 cbcb cb6b
  //   cb2d cb6e cbee cb23 cbef cb2f 6be7 6b21 6bcb 6b6b 6b2d 6b6e 6bee 6b23 6bef 6b2f 2de7 2d21 2dcb 2d6b
  //   2d2d 2d6e 2dee 2d23 2def 2d2f 6ee7 6e21 6ecb 6e6b 6e2d 6e6e 6eee 6e23 6eef 6e2f eee7 ee21 eecb ee6b
  //   ee2d ee6e eeee ee23 eeef ee2f 23e7 2321 23cb 236b 232d 236e 23ee 2323 23ef 232f efe7 ef21 efcb ef6b
  //   ef2d ef6e efee ef23 efef ef2f 2fe7 2f21 2fcb 2f6b 2f2d 2f6e 2fee 2f23 2fef 2f2f 21e7e7 21e721 21e7cb
  //   21e76b 21e72d 21e76e 21e7ee 21e723 21e7ef 21e72f 2121e7 212121 2121cb 21216b 21212d 21216e 2121ee
  //   212123 2121ef 21212f 21cbe7 21cb21 21cbcb 21cb6b 21cb2d 21cb6e 21cbee 21cb23 21cbef 21cb2f 216be7
  //   216b21 216bcb 216b6b 216b2d 216b6e 216bee 216b23 216bef 216b2f 212de7 212d21 212dcb 212d6b 212d2d
  //   212d6e 212dee 212d23 212def 212d2f 216ee7 216e21 216ecb 216e6b 216e2d 216e6e 216eee 216e23 216eef
  //   216e2f 21eee7 21ee21 21eecb 21ee6b 21ee2d 21ee6e 21eeee 21ee23 21eeef 21ee2f 2123e7 212321 2123cb
  //   21236b 21232d 21236e 2123ee 212323 2123ef 21232f 21efe7 21ef21 21efcb 21ef6b 21ef2d 21ef6e 21efee
  //   21ef23 21efef 21ef2f 212fe7 212f21 212fcb 212f6b 212f2d 212f6e 212fee 212f23 212fef 212f2f cbe7e7
  //   cbe721 cbe7cb cbe76b cbe72d cbe76e cbe7ee cbe723 cbe7ef cbe72f cb21e7 cb2121 cb21cb cb216b cb212d
  //   cb216e cb21ee cb2123 cb21ef cb212f cbcbe7 cbcb21 cbcbcb cbcb6b cbcb2d cbcb6e cbcbee cbcb23 cbcbef
  //   cbcb2f cb6be7 cb6b21 cb6bcb cb6b6b cb6b2d cb6b6e cb6bee cb6b23 cb6bef cb6b2f cb2de7 cb2d21 cb2dcb
  //   cb2d6b cb2d2d cb2d6e cb2dee cb2d23 cb2def cb2d2f cb6ee7 cb6e21 cb6ecb cb6e6b cb6e2d cb6e6e cb6eee
  //   cb6e23 cb6eef cb6e2f cbeee7 cbee21 cbeecb cbee6b cbee2d cbee6e cbeeee cbee23 cbeeef cbee2f cb23e7
  //   cb2321 cb23cb cb236b cb232d cb236e cb23ee cb2323 cb23ef cb232f cbefe7 cbef21 cbefcb cbef6b cbef2d
  //   cbef6e cbefee cbef23 cbefef cbef2f cb2fe7 cb2f21 cb2fcb cb2f6b cb2f2d cb2f6e cb2fee cb2f23 cb2fef
  //   cb2f2f 6be7e7 6be721 6be7cb 6be76b 6be72d 6be76e 6be7ee 6be723 6be7ef 6be72f 6b21e7 6b2121 6b21cb
  //   6b216b 6b212d 6b216e 6b21ee 6b2123 6b21ef 6b212f 6bcbe7 6bcb21 6bcbcb 6bcb6b 6bcb2d 6bcb6e 6bcbee
  //   6bcb23 6bcbef 6bcb2f 6b6be7 6b6b21 6b6bcb 6b6b6b 6b6b2d 6b6b6e 6b6bee 6b6b23 6b6bef 6b6b2f 6b2de7
  //   6b2d21 6b2dcb 6b2d6b 6b2d2d 6b2d6e 6b2dee 6b2d23 6b2def 6b2d2f 6b6ee7 6b6e21 6b6ecb 6b6e6b 6b6e2d
  //   6b6e6e 6b6eee 6b6e23 6b6eef 6b6e2f 6beee7 6bee21 6beecb 6bee6b 6bee2d 6bee6e 6beeee 6bee23 6beeef
  //   6bee2f 6b23e7 6b2321 6b23cb 6b236b 6b232d 6b236e 6b23ee 6b2323 6b23ef 6b232f 6befe7 6bef21 6befcb
  //   6bef6b 6bef2d 6bef6e 6befee 6bef23 6befef 6bef2f 6b2fe7 6b2f21 6b2fcb 6b2f6b 6b2f2d 6b2f6e 6b2fee
  //   6b2f23 6b2fef 6b2f2f 2de7e7 2de721 2de7cb 2de76b 2de72d 2de76e 2de7ee 2de723 2de7ef 2de72f 2d21e7
  //   2d2121 2d21cb 2d216b 2d212d 2d216e 2d21ee 2d2123 2d21ef 2d212f 2dcbe7 2dcb21 2dcbcb 2dcb6b 2dcb2d
  //   2dcb6e 2dcbee 2dcb23 2dcbef 2dcb2f 2d6be7 2d6b21 2d6bcb 2d6b6b 2d6b2d 2d6b6e 2d6bee 2d6b23 2d6bef
  //   2d6b2f 2d2de7 2d2d21 2d2dcb 2d2d6b 2d2d2d 2d2d6e 2d2dee 2d2d23 2d2def 2d2d2f 2d6ee7 2d6e21 2d6ecb
  //   2d6e6b 2d6e2d 2d6e6e 2d6eee 2d6e23 2d6eef 2d6e2f 2deee7 2dee21 2deecb 2dee6b 2dee2d 2dee6e 2deeee
  //   2dee23 2deeef 2dee2f 2d23e7 2d2321 2d23cb 2d236b 2d232d 2d236e 2d23ee 2d2323 2d23ef 2d232f 2defe7
  //   2def21 2defcb 2def6b 2def2d 2def6e 2defee 2def23 2defef 2def2f 2d2fe7 2d2f21 2d2fcb 2d2f6b 2d2f2d
  //   2d2f6e 2d2fee 2d2f23 2d2fef 2d2f2f 6ee7e7 6ee721 6ee7cb 6ee76b 6ee72d 6ee76e 6ee7ee 6ee723 6ee7ef
  //   6ee72f 6e21e7 6e2121 6e21cb 6e216b 6e212d 6e216e 6e21ee 6e2123 6e21ef 6e212f 6ecbe7 6ecb21 6ecbcb
  //   6ecb6b 6ecb2d 6ecb6e 6ecbee 6ecb23 6ecbef 6ecb2f 6e6be7 6e6b21 6e6bcb 6e6b6b 6e6b2d 6e6b6e 6e6bee
  //   6e6b23 6e6bef 6e6b2f 6e2de7 6e2d21 6e2dcb 6e2d6b 6e2d2d 6e2d6e 6e2dee 6e2d23 6e2def 6e2d2f 6e6ee7
  //   6e6e21 6e6ecb 6e6e6b 6e6e2d 6e6e6e 6e6eee 6e6e23 6e6eef 6e6e2f 6eeee7 6eee21 6eeecb 6eee6b 6eee2d
  //   6eee6e 6eeeee 6eee23 6eeeef 6eee2f 6e23e7 6e2321 6e23cb 6e236b 6e232d 6e236e 6e23ee 6e2323 6e23ef
  //   6e232f 6eefe7 6eef21 6eefcb 6eef6b 6eef2d 6eef6e 6eefee 6eef23 6eefef 6eef2f 6e2fe7 6e2f21 6e2fcb
  //   6e2f6b 6e2f2d 6e2f6e 6e2fee 6e2f23 6e2fef 6e2f2f eee7e7 eee721 eee7cb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
endmodule

module CPU (
  input  [15:0] in_1,
  input  OE_TestingData,
  input  RESET_MAR,
  input  Reset_IR,
  input  RESET_MBR,
  input  Reset_A,
  input  OE_A,
  input  RESET_OR,
  input  [2:0] ro_selector,
  input  AO_Enable,
  input  [3:0] ao_selector,
  input  Borrow_in,
  input  Carry_in,
  input  Alu_selector,
  input  Reset_B,
  input  OE_B,
  output [7:0] Content_MAR,
  output [7:0] Content_Counter,
  output [15:0] Content_IR,
  output [15:0] Content_MBR,
  output [15:0] Dout_IR,
  output [3:0] out_22,
  output [15:0] Content_A,
  output [15:0] Dout_A,
  output [15:0] Content_Output,
  output [2:0] out_26,
  output out_27,
  output [15:0] Content_B,
  output [15:0] Dout_B
);

  wire CLK_out, cu_1_c0, cu_1_c1, cu_1_c2, cu_1_c3, cu_1_c4, cu_1_c5, cu_1_c6, cu_1_c7, cu_1_c8, cu_1_c9,
       cu_1_c10, cu_1_c12, cu_1_c13, cu_1_c14, cu_1_c15;
  wire [7:0] controlled_buffer_1_out, controlled_buffer_7_out;
  wire [15:0] bit_extender_1_out, bit_extender_2_out, project_alu_1_ao_dout, project_alu_1_final_result,
       ram_1_dout;
  wire [31:0] decimaldecoder_1_dout, decimaldecoder_2_dout, decimaldecoder_3_dout, decimaldecoder_4_dout,
       decimaldecoder_5_dout, decimaldecoder_6_dout, decimaldecoder_7_dout;

  Clock CLK (.out(CLK_out));
  Counter #(.max('h3)) Program_Counter (
    .count(cu_1_c1), .clk(CLK_out), .D(controlled_buffer_1_out), .Q(Content_Counter));  // open: clr, load, up, carry
  Register #(.width(16)) Instruction_Register (
    .D(project_alu_1_ao_dout), .en(cu_1_c7), .clk(CLK_out), .Q(Content_IR), .clr(Reset_IR));
  Register #(.width(16)) Register_A (
    .D(project_alu_1_ao_dout), .en(cu_1_c12), .clk(CLK_out), .Q(Content_A), .clr(Reset_A));
  Register #(.width(16)) Register_B (
    .D(project_alu_1_ao_dout), .en(cu_1_c13), .clk(CLK_out), .Q(Content_B), .clr(Reset_B));
  assign controlled_buffer_1_out = cu_1_c0 ? Content_Counter : 8'bz;  // Controlled_Buffer controlled_buffer_1
  assign Dout_IR = cu_1_c8 ? Content_IR : 16'bz;  // Controlled_Buffer controlled_buffer_2
  assign Dout_A = OE_A ? Content_A : 16'bz;  // Controlled_Buffer controlled_buffer_3
  assign Dout_B = OE_B ? Content_B : 16'bz;  // Controlled_Buffer controlled_buffer_4
  BitSelector #(.group(8), .width(16)) bitselector_1 (.in(Dout_IR), .out(controlled_buffer_1_out), .sel(1'b0));
  assign bit_extender_1_out = {{8{1'b0}}, Content_Counter};  // Bit_Extender bit_extender_1
  Decimaldecoder decimaldecoder_1 (.Din(bit_extender_1_out), .Dout(decimaldecoder_1_dout));
  project_alu project_alu_1 (
    .NOTHING(1'b0), .RO_SELECT(ro_selector), .INPUT_A(Content_A), .INPUT_B(Content_B), .OP_CODE(ao_selector),
    .CARRY_IN(Carry_in), .BORROW_IN(Borrow_in), .ALU_SELECTOR(Alu_selector), .AOEnable(AO_Enable),
    .FINAL_RESULT(project_alu_1_final_result), .AO_DOUT(project_alu_1_ao_dout), .zeroflag(out_27));  // open: RORESULT, AORESULT
  Decimaldecoder decimaldecoder_2 (.Din(Content_B), .Dout(decimaldecoder_2_dout));
  _7_Segment_Display u_7_segment_display_1 (
    .g(decimaldecoder_1_dout[3]), .f(decimaldecoder_1_dout[2]), .a(decimaldecoder_1_dout[1]),
    .b(decimaldecoder_1_dout[0]), .e(decimaldecoder_1_dout[19]), .d(decimaldecoder_1_dout[18]),
    .c(decimaldecoder_1_dout[17]), .dp(decimaldecoder_1_dout[16]));
  _7_Segment_Display u_7_segment_display_2 (
    .g(decimaldecoder_3_dout[15]), .f(decimaldecoder_3_dout[14]), .a(decimaldecoder_3_dout[13]),
    .b(decimaldecoder_3_dout[12]), .e(decimaldecoder_3_dout[31]), .d(decimaldecoder_3_dout[30]),
    .c(decimaldecoder_3_dout[29]), .dp(decimaldecoder_3_dout[28]));
  Decimaldecoder decimaldecoder_3 (.Din(Content_IR), .Dout(decimaldecoder_3_dout));
  Decimaldecoder decimaldecoder_4 (.Din(Content_A), .Dout(decimaldecoder_4_dout));
  _7_Segment_Display u_7_segment_display_3 (
    .g(decimaldecoder_2_dout[15]), .f(decimaldecoder_2_dout[14]), .a(decimaldecoder_2_dout[13]),
    .b(decimaldecoder_2_dout[12]), .e(decimaldecoder_2_dout[31]), .d(decimaldecoder_2_dout[30]),
    .c(decimaldecoder_2_dout[29]), .dp(decimaldecoder_2_dout[28]));
  _7_Segment_Display u_7_segment_display_4 (
    .g(decimaldecoder_2_dout[11]), .f(decimaldecoder_2_dout[10]), .a(decimaldecoder_2_dout[9]),
    .b(decimaldecoder_2_dout[8]), .e(decimaldecoder_2_dout[27]), .d(decimaldecoder_2_dout[26]),
    .c(decimaldecoder_2_dout[25]), .dp(decimaldecoder_2_dout[24]));
  _7_Segment_Display u_7_segment_display_5 (
    .g(decimaldecoder_3_dout[11]), .f(decimaldecoder_3_dout[10]), .a(decimaldecoder_3_dout[9]),
    .b(decimaldecoder_3_dout[8]), .e(decimaldecoder_3_dout[27]), .d(decimaldecoder_3_dout[26]),
    .c(decimaldecoder_3_dout[25]), .dp(decimaldecoder_3_dout[24]));
  _7_Segment_Display u_7_segment_display_6 (
    .g(decimaldecoder_3_dout[7]), .f(decimaldecoder_3_dout[6]), .a(decimaldecoder_3_dout[5]),
    .b(decimaldecoder_3_dout[4]), .e(decimaldecoder_3_dout[23]), .d(decimaldecoder_3_dout[22]),
    .c(decimaldecoder_3_dout[21]), .dp(decimaldecoder_3_dout[20]));
  _7_Segment_Display u_7_segment_display_7 (
    .g(decimaldecoder_4_dout[15]), .f(decimaldecoder_4_dout[14]), .a(decimaldecoder_4_dout[13]),
    .b(decimaldecoder_4_dout[12]), .e(decimaldecoder_4_dout[31]), .d(decimaldecoder_4_dout[30]),
    .c(decimaldecoder_4_dout[29]), .dp(decimaldecoder_4_dout[28]));
  _7_Segment_Display u_7_segment_display_8 (
    .g(decimaldecoder_4_dout[11]), .f(decimaldecoder_4_dout[10]), .a(decimaldecoder_4_dout[9]),
    .b(decimaldecoder_4_dout[8]), .e(decimaldecoder_4_dout[27]), .d(decimaldecoder_4_dout[26]),
    .c(decimaldecoder_4_dout[25]), .dp(decimaldecoder_4_dout[24]));
  _7_Segment_Display u_7_segment_display_9 (
    .g(decimaldecoder_5_dout[15]), .f(decimaldecoder_5_dout[14]), .a(decimaldecoder_5_dout[13]),
    .b(decimaldecoder_5_dout[12]), .e(decimaldecoder_5_dout[31]), .d(decimaldecoder_5_dout[30]),
    .c(decimaldecoder_5_dout[29]), .dp(decimaldecoder_5_dout[28]));
  _7_Segment_Display u_7_segment_display_10 (
    .g(decimaldecoder_2_dout[7]), .f(decimaldecoder_2_dout[6]), .a(decimaldecoder_2_dout[5]),
    .b(decimaldecoder_2_dout[4]), .e(decimaldecoder_2_dout[23]), .d(decimaldecoder_2_dout[22]),
    .c(decimaldecoder_2_dout[21]), .dp(decimaldecoder_2_dout[20]));
  _7_Segment_Display u_7_segment_display_11 (
    .g(decimaldecoder_2_dout[3]), .f(decimaldecoder_2_dout[2]), .a(decimaldecoder_2_dout[1]),
    .b(decimaldecoder_2_dout[0]), .e(decimaldecoder_2_dout[19]), .d(decimaldecoder_2_dout[18]),
    .c(decimaldecoder_2_dout[17]), .dp(decimaldecoder_2_dout[16]));
  _7_Segment_Display u_7_segment_display_12 (
    .g(decimaldecoder_3_dout[3]), .f(decimaldecoder_3_dout[2]), .a(decimaldecoder_3_dout[1]),
    .b(decimaldecoder_3_dout[0]), .e(decimaldecoder_3_dout[19]), .d(decimaldecoder_3_dout[18]),
    .c(decimaldecoder_3_dout[17]), .dp(decimaldecoder_3_dout[16]));
  _7_Segment_Display u_7_segment_display_13 (
    .g(decimaldecoder_4_dout[7]), .f(decimaldecoder_4_dout[6]), .a(decimaldecoder_4_dout[5]),
    .b(decimaldecoder_4_dout[4]), .e(decimaldecoder_4_dout[23]), .d(decimaldecoder_4_dout[22]),
    .c(decimaldecoder_4_dout[21]), .dp(decimaldecoder_4_dout[20]));
  _7_Segment_Display u_7_segment_display_14 (
    .g(decimaldecoder_4_dout[3]), .f(decimaldecoder_4_dout[2]), .a(decimaldecoder_4_dout[1]),
    .b(decimaldecoder_4_dout[0]), .e(decimaldecoder_4_dout[19]), .d(decimaldecoder_4_dout[18]),
    .c(decimaldecoder_4_dout[17]), .dp(decimaldecoder_4_dout[16]));
  _7_Segment_Display u_7_segment_display_15 (
    .g(decimaldecoder_5_dout[11]), .f(decimaldecoder_5_dout[10]), .a(decimaldecoder_5_dout[9]),
    .b(decimaldecoder_5_dout[8]), .e(decimaldecoder_5_dout[27]), .d(decimaldecoder_5_dout[26]),
    .c(decimaldecoder_5_dout[25]), .dp(decimaldecoder_5_dout[24]));
  _7_Segment_Display u_7_segment_display_16 (
    .g(decimaldecoder_5_dout[7]), .f(decimaldecoder_5_dout[6]), .a(decimaldecoder_5_dout[5]),
    .b(decimaldecoder_5_dout[4]), .e(decimaldecoder_5_dout[23]), .d(decimaldecoder_5_dout[22]),
    .c(decimaldecoder_5_dout[21]), .dp(decimaldecoder_5_dout[20]));
  Decimaldecoder decimaldecoder_5 (.Din(project_alu_1_final_result), .Dout(decimaldecoder_5_dout));
  _7_Segment_Display u_7_segment_display_17 (
    .g(decimaldecoder_5_dout[3]), .f(decimaldecoder_5_dout[2]), .a(decimaldecoder_5_dout[1]),
    .b(decimaldecoder_5_dout[0]), .e(decimaldecoder_5_dout[19]), .d(decimaldecoder_5_dout[18]),
    .c(decimaldecoder_5_dout[17]), .dp(decimaldecoder_5_dout[16]));
  LED D15 (.in(project_alu_1_ao_dout[15]));
  LED D14 (.in(project_alu_1_ao_dout[14]));
  LED D13 (.in(project_alu_1_ao_dout[13]));
  LED D12 (.in(project_alu_1_ao_dout[12]));
  LED D11 (.in(project_alu_1_ao_dout[11]));
  assign project_alu_1_ao_dout = OE_TestingData ? in_1 : 16'bz;  // Controlled_Buffer controlled_buffer_5
  LED D10 (.in(project_alu_1_ao_dout[10]));
  LED D9 (.in(project_alu_1_ao_dout[9]));
  LED D8 (.in(project_alu_1_ao_dout[8]));
  LED D7 (.in(project_alu_1_ao_dout[7]));
  LED D6 (.in(project_alu_1_ao_dout[6]));
  LED D5 (.in(project_alu_1_ao_dout[5]));
  LED D4 (.in(project_alu_1_ao_dout[4]));
  LED D3 (.in(project_alu_1_ao_dout[3]));
  LED D2 (.in(project_alu_1_ao_dout[2]));
  LED D1 (.in(project_alu_1_ao_dout[1]));
  LED D0 (.in(project_alu_1_ao_dout[0]));
  Register Memory_Address_Register (
    .D(controlled_buffer_1_out), .en(cu_1_c9), .clk(CLK_out), .Q(Content_MAR), .clr(RESET_MAR));
  assign project_alu_1_ao_dout = cu_1_c5 ? Content_MBR : 16'bz;  // Controlled_Buffer controlled_buffer_6
  Register #(.width(16)) Memory_Buffer_Register (
    .D(project_alu_1_ao_dout), .en(cu_1_c4), .clk(CLK_out), .Q(Content_MBR), .clr(RESET_MBR));
  Register #(.width(16)) Output_Register (
    .D(project_alu_1_ao_dout), .en(cu_1_c15), .clk(CLK_out), .Q(Content_Output), .clr(RESET_OR));
  assign controlled_buffer_7_out = cu_1_c10 ? Content_MAR : 8'bz;  // Controlled_Buffer controlled_buffer_7
  assign project_alu_1_ao_dout = cu_1_c6 ? Content_MBR : 16'bz;  // Controlled_Buffer controlled_buffer_8
  assign project_alu_1_ao_dout = cu_1_c14 ? Content_Output : 16'bz;  // Controlled_Buffer controlled_buffer_9
  _7_Segment_Display u_7_segment_display_18 (
    .g(decimaldecoder_6_dout[15]), .f(decimaldecoder_6_dout[14]), .a(decimaldecoder_6_dout[13]),
    .b(decimaldecoder_6_dout[12]), .e(decimaldecoder_6_dout[31]), .d(decimaldecoder_6_dout[30]),
    .c(decimaldecoder_6_dout[29]), .dp(decimaldecoder_6_dout[28]));
  Decimaldecoder decimaldecoder_6 (.Din(Content_Output), .Dout(decimaldecoder_6_dout));
  _7_Segment_Display u_7_segment_display_19 (
    .g(decimaldecoder_6_dout[11]), .f(decimaldecoder_6_dout[10]), .a(decimaldecoder_6_dout[9]),
    .b(decimaldecoder_6_dout[8]), .e(decimaldecoder_6_dout[27]), .d(decimaldecoder_6_dout[26]),
    .c(decimaldecoder_6_dout[25]), .dp(decimaldecoder_6_dout[24]));
  _7_Segment_Display u_7_segment_display_20 (
    .g(decimaldecoder_6_dout[7]), .f(decimaldecoder_6_dout[6]), .a(decimaldecoder_6_dout[5]),
    .b(decimaldecoder_6_dout[4]), .e(decimaldecoder_6_dout[23]), .d(decimaldecoder_6_dout[22]),
    .c(decimaldecoder_6_dout[21]), .dp(decimaldecoder_6_dout[20]));
  LED led_1 (.in(project_alu_1_ao_dout[15]));
  _7_Segment_Display u_7_segment_display_21 (
    .g(decimaldecoder_6_dout[3]), .f(decimaldecoder_6_dout[2]), .a(decimaldecoder_6_dout[1]),
    .b(decimaldecoder_6_dout[0]), .e(decimaldecoder_6_dout[19]), .d(decimaldecoder_6_dout[18]),
    .c(decimaldecoder_6_dout[17]), .dp(decimaldecoder_6_dout[16]));
  LED led_2 (.in(project_alu_1_ao_dout[14]));
  LED led_3 (.in(project_alu_1_ao_dout[13]));
  LED led_4 (.in(project_alu_1_ao_dout[12]));
  LED led_5 (.in(project_alu_1_ao_dout[11]));
  LED led_6 (.in(project_alu_1_ao_dout[10]));
  LED led_7 (.in(project_alu_1_ao_dout[9]));
  LED led_8 (.in(project_alu_1_ao_dout[8]));
  LED led_9 (.in(project_alu_1_ao_dout[7]));
  LED led_10 (.in(project_alu_1_ao_dout[6]));
  LED led_11 (.in(project_alu_1_ao_dout[5]));
  LED led_12 (.in(project_alu_1_ao_dout[4]));
  LED led_13 (.in(project_alu_1_ao_dout[3]));
  LED led_14 (.in(project_alu_1_ao_dout[2]));
  LED led_15 (.in(project_alu_1_ao_dout[1]));
  LED led_16 (.in(project_alu_1_ao_dout[0]));
  RAM #(.clearpin("true"), .dataWidth(16), .enables("line")) ram_1 (
    .addr(controlled_buffer_7_out), .we(cu_1_c2), .clk(CLK_out), .din(project_alu_1_ao_dout),
    .dout(ram_1_dout));  // open: clr
  BitSelector #(.group(4), .width(16)) bitselector_2 (.in(Content_IR), .out(out_22), .sel(2'b10));
  Counter #(.max('h5), .width(3)) StepCounter (.clk(CLK_out), .Q(out_26));  // open: clr, load, up, count, D, carry
  assign project_alu_1_ao_dout = cu_1_c3 ? ram_1_dout : 16'bz;  // Controlled_Buffer controlled_buffer_10
  assign bit_extender_2_out = {{13{1'b0}}, out_26};  // Bit_Extender bit_extender_2
  Decimaldecoder decimaldecoder_7 (.Din(bit_extender_2_out), .Dout(decimaldecoder_7_dout));
  CU cu_1 (
    .OPC3(out_22[3]), .OPC2(out_22[2]), .OPC1(out_22[1]), .OPC0(out_22[0]), .SC2(out_26[2]), .SC1(out_26[1]),
    .SC0(out_26[0]), .C0(cu_1_c0), .C1(cu_1_c1), .C2(cu_1_c2), .C3(cu_1_c3), .C4(cu_1_c4), .C5(cu_1_c5),
    .C6(cu_1_c6), .C7(cu_1_c7), .C8(cu_1_c8), .C9(cu_1_c9), .C10(cu_1_c10), .C11(AO_Enable), .C12(cu_1_c12),
    .C13(cu_1_c13), .C14(cu_1_c14), .C15(cu_1_c15));
  _7_Segment_Display u_7_segment_display_22 (
    .g(decimaldecoder_7_dout[3]), .f(decimaldecoder_7_dout[2]), .a(decimaldecoder_7_dout[1]),
    .b(decimaldecoder_7_dout[0]), .e(decimaldecoder_7_dout[19]), .d(decimaldecoder_7_dout[18]),
    .c(decimaldecoder_7_dout[17]), .dp(decimaldecoder_7_dout[16]));

  // Notes on the sheet:
  //   INTERNAL DATA BUS (8 BITS)
  //   INTERNAL DATA BUS
  //   EXTERNAL DATA BUS (8 BITS)
  //   EXTERNAL DATA BUS
  //   C12
  //   C11
  //   C10
  //   C9
  //   C8
  //   C7
  //   C6
  //   C5
  //   C4
  //   C3
  //   C2
  //   C1
  //   C0
  //   C15
  //   C14
  //   C13
endmodule

module CU (
  input  OPC3,
  input  OPC2,
  input  OPC1,
  input  OPC0,
  input  SC2,
  input  SC1,
  input  SC0,
  output C0,
  output C1,
  output C2,
  output C3,
  output C4,
  output C5,
  output C6,
  output C7,
  output C8,
  output C9,
  output C10,
  output C11,
  output C12,
  output C13,
  output C14,
  output C15
);

  wire and_4_out, and_5_out, and_6_out, and_7_out, and_8_out, and_9_out, and_10_out, and_13_out, and_14_out,
       and_15_out, and_16_out, and_17_out, and_18_out, and_19_out, and_20_out, not_1_out, not_2_out,
       not_3_out, not_4_out, not_5_out;

  not not_1 (not_1_out, OPC1);
  not not_2 (not_2_out, OPC0);
  not not_3 (not_3_out, SC2);
  not not_4 (not_4_out, SC1);
  not not_5 (not_5_out, SC0);
  and and_1 (C0, not_3_out, not_4_out, not_5_out);
  and and_2 (C1, not_3_out, not_4_out, SC0);
  and and_3 (C2, OPC1, OPC0, SC2, not_4_out, not_5_out);
  and and_4 (and_4_out, not_3_out, not_4_out, SC0);
  and and_5 (and_5_out, not_1_out, SC2, not_4_out, not_5_out);
  and and_6 (and_6_out, not_3_out, not_4_out, SC0);
  and and_7 (and_7_out, not_1_out, SC2, not_4_out, not_5_out);
  and and_8 (and_8_out, OPC1, OPC0, not_3_out, SC0);
  and and_9 (and_9_out, not_3_out, SC1, not_5_out);
  and and_10 (and_10_out, not_1_out, SC2, not_4_out, SC0);
  and and_11 (C6, OPC1, OPC0, SC2, not_4_out, not_5_out);
  and and_12 (C7, not_3_out, SC1, not_5_out);
  and and_13 (and_13_out, not_1_out, not_3_out, SC1, SC0);
  and and_14 (and_14_out, OPC0, not_3_out, SC1, SC0);
  and and_15 (and_15_out, not_3_out, not_4_out, not_5_out);
  and and_16 (and_16_out, not_1_out, not_3_out, SC1, SC0);
  and and_17 (and_17_out, OPC0, not_3_out, SC1, SC0);
  and and_18 (and_18_out, not_3_out, not_4_out, SC0);
  and and_19 (and_19_out, not_1_out, SC2, not_4_out, not_5_out);
  and and_20 (and_20_out, OPC0, SC2, not_4_out, not_5_out);
  and and_21 (C11, OPC1, not_2_out, not_3_out, SC1, SC0);
  and and_22 (C12, not_1_out, not_2_out, SC2, not_4_out, SC0);
  and and_23 (C13, not_1_out, OPC0, SC2, not_4_out, SC0);
  and and_24 (C14, OPC1, OPC0, not_3_out, SC1, SC0);
  and and_25 (C15, OPC1, not_2_out, not_3_out, SC1, SC0);
  or or_1 (C3, and_4_out, and_5_out);
  or or_2 (C4, and_6_out, and_7_out, and_8_out);
  or or_3 (C5, and_9_out, and_10_out);
  or or_4 (C8, and_13_out, and_14_out);
  or or_5 (C9, and_15_out, and_16_out, and_17_out);
  or or_6 (C10, and_18_out, and_19_out, and_20_out);
endmodule
